// Logisim project alu.circ as structural Verilog
module alu (
  input  [3:0] opr_0,
  input  [3:0] opr_1,
  input  En,
  input  [2:0] OP,
  output ZF,
  output [3:0] O
);

  wire decoder_1_out0, decoder_1_out1, decoder_1_out2, decoder_1_out3, decoder_1_out4;
  wire [3:0] adder_1_out, and_1_out, or_1_out, subtractor_1_out, xor_1_out;

  Decoder #(.select(3)) decoder_1 (
    .out0(decoder_1_out0), .out1(decoder_1_out1), .out2(decoder_1_out2), .out3(decoder_1_out3),
    .out4(decoder_1_out4), .sel(OP), .en(En));  // open: out5, out6, out7
  assign O = decoder_1_out0 ? adder_1_out : 4'bz;  // Controlled_Buffer controlled_buffer_1
  Adder #(.width(4)) adder_1 (.a(opr_0), .b(opr_1), .out(adder_1_out));  // open: cin, cout
  assign O = decoder_1_out1 ? subtractor_1_out : 4'bz;  // Controlled_Buffer controlled_buffer_2
  Subtractor #(.width(4)) subtractor_1 (.a(opr_0), .b(opr_1), .out(subtractor_1_out));  // open: bin, bout
  assign O = decoder_1_out2 ? and_1_out : 4'bz;  // Controlled_Buffer controlled_buffer_3
  assign and_1_out = opr_0 & opr_1;  // AND_Gate and_1, 4 bits wide
  assign O = decoder_1_out3 ? or_1_out : 4'bz;  // Controlled_Buffer controlled_buffer_4
  assign or_1_out = opr_0 | opr_1;  // OR_Gate or_1, 4 bits wide
  assign O = decoder_1_out4 ? xor_1_out : 4'bz;  // Controlled_Buffer controlled_buffer_5
  assign xor_1_out = opr_0 ^ opr_1;  // XOR_Gate xor_1, 4 bits wide
  nor nor_1 (ZF, O[0], O[1], O[2], O[3]);

  // Notes on the sheet:
  //   ADD = 000
  //   SUB = 001
  //   AND = 010
  //   OR = 011
  //   X-OR = 100
endmodule
